# Fritzing sketch circuit diagram (saved by Fritzing 0.9.3b)
breadboards: 1

parts:
  Raspberry_Pi_1 = Raspberry Pi 3 [part_number=RPI-3-V1.2]
  R1 = Resistor [tolerance=±5% resistance=220 package="0805 [SMD]"]
  LED2 = LED - 5mm [color="Red (633nm)" package="5 mm [THT]"]
  PIR2 = PIR sensor

nets:
  N1: Raspberry_Pi_1.GPIO17, PIR2.SIG
  N2: Raspberry_Pi_1.GPIO27, LED2.anode
  GND: Raspberry_Pi_1.GND, PIR2.GND
  5V: Raspberry_Pi_1.5V, PIR2.VDD
  N3: R1.Pin_0, LED2.cathode
